# Fritzing sketch Useless-Box-Shield-v1 (saved by Fritzing 1.0.4)
circuit board: 2.54527cm x 3.0382cm

parts:
  Useless_Box_Shield = WeMos D1 Mini Protoboard Shield
  R1 = Resistor [tolerance=±5% resistance=1k power=0.25W package=THT]
  Arm_Servo = Dagu DGServo 9g header (male) [part_number=Arm package=THT]
  Lid_Servo = Dagu DGServo 9g header (male) [part_number=Lid package=THT]
  Sensor = male pin header, 5 pins [form="♂ (male)"]
  Switch = male pin header, 2 pins [form="♂ (male)"]

nets:
  N1: Useless_Box_Shield.3V3, Useless_Box_Shield.X2-Y8, R1.Pin_1, Sensor.pin2
  VCC: Useless_Box_Shield.5V, Arm_Servo.Vcc, Lid_Servo.Vcc
  N2: Useless_Box_Shield.D0, Useless_Box_Shield.X2-Y3, Arm_Servo.pulse
  N3: Useless_Box_Shield.D1, Useless_Box_Shield.X7-Y3, Sensor.pin4
  N4: Useless_Box_Shield.D2, Useless_Box_Shield.X7-Y4, Sensor.pin3
  N5: Useless_Box_Shield.D5, Useless_Box_Shield.X2-Y4, R1.Pin_0, Switch.pin1
  N6: Useless_Box_Shield.D6, Sensor.pin5
  N7: Useless_Box_Shield.D8, Useless_Box_Shield.X2-Y7, Lid_Servo.pulse
  GND: Useless_Box_Shield.G, Useless_Box_Shield.X7-Y7, Arm_Servo.gnd, Lid_Servo.gnd, Sensor.pin1, Switch.pin2

notes:
  Useless Box Shield v1
  GND
  VCC
  SDA
  SCL
  INT
  5V
  3V3
  TX
  RST
