# Fritzing sketch Useless-Box-Shield-v2 (saved by Fritzing 1.0.4)
breadboards: 1

parts:
  A1 = esp32-c3-super-mini-smd_1
  SERVO-LID-ARM = Tower Pro SG90 servo [part_number=101246]
  SERVO-SWITCH-ARM = Tower Pro SG90 servo [part_number=101246]
  S1 = Toggle Switch spst [package=THT]
  R1 = Resistor [tolerance=±5% power=0.25W resistance=1000 package=THT]
  PART1 = APDS-9960 RGB and Gesture Sensor [part_number=SEN-12787]

nets:
  N1: A1.connector1, PART1.SDA
  N2: A1.connector2, PART1.SCL
  N3: A1.connector4, PART1.INT
  N4: A1.connector8, SERVO-SWITCH-ARM.Signal
  N5: A1.connector10, SERVO-LID-ARM.Signal
  N6: A1.connector11, S1.L1, R1.Pin_0
  N7: A1.connector13, R1.Pin_1, PART1.VCC
  GND: A1.connector14, SERVO-LID-ARM.GND, SERVO-SWITCH-ARM.GND, S1.COM, PART1.GND
  +5V: A1.connector15, SERVO-LID-ARM.+5V, SERVO-SWITCH-ARM.+5V

custom parts:
  Tower Pro SG90 servo: Original file by John De Cristofaro http://www.adafruit.com/products/1449 Adafruit Feedback Servo (Small) Edited by: e-radionica.com 28/9/2015
  Toggle Switch spst: Toggle Switch single pole single throw
  APDS-9960 RGB and Gesture Sensor: Breakout board for the Avago APDS-9960 proximity, light, RGB, and gesture sensors. Please visit www.sparkfun.com to learn more.
